// Logisim project Project2Given (1).circ as structural Verilog: 4 circuits, main circuit main
module main (
);

  wire and_1_out, and_2_out, B0, B1, B2, B3, B4, B5, B6, B7, B8, B9, BL, BU, C0, C1, C2, CLK, L1_p8, L1_p9,
       not_1_out, or_9_out, P1_v, R0, R1, R3, R4, Valid;
  wire [2:0] counter_1_q;
  wire [3:0] IB1_c0, P1_b0, register_2_q, register_3_q, register_4_q, register_5_q;

  Button n1 (.out(B1));
  Button n4 (.out(B4));
  Button n7 (.out(B7));
  Button L (.out(BL));
  Button n3 (.out(B3));
  Button n2 (.out(B2));
  Button n6 (.out(B6));
  Button n5 (.out(B5));
  Button n9 (.out(B9));
  Button n8 (.out(B8));
  Button U (.out(BU));
  Button n0 (.out(B0));
  or or_1 (R0, B3, B2, B1);
  or or_2 (R1, B6, B5, B4);
  or or_3 (R3, B9, B8, B7);
  or or_4 (R4, BU, B0, BL);
  or or_5 (C0, B1, B4, B7, BL);
  or or_6 (C1, B2, B5, B8, B0);
  or or_7 (C2, B3, B6, B9, BU);
  // OR_Gate or_8 is placed but not wired
  Clock clock_1 (.out(CLK));
  nand nand_1 (Valid, IB1_c0[0], IB1_c0[1], IB1_c0[2], IB1_c0[3]);
  // Probe on P1_b0
  Panel P1 (
    .R0(R0), .R1(R1), .R2(R3), .R3(R4), .C0(C0), .C1(C1), .C2(C2), .B0(P1_b0[0]), .B1(P1_b0[1]),
    .B2(P1_b0[2]), .B3(P1_b0[3]), .V(P1_v));
  LED Press (.in(P1_v));
  // Probe on IB1_c0
  InputBuffer IB1 (
    .B0(P1_b0[0]), .B1(P1_b0[1]), .B2(P1_b0[2]), .B3(P1_b0[3]), .V(P1_v), .CLK(not_1_out), .C0(IB1_c0[0]),
    .C1(IB1_c0[1]), .C2(IB1_c0[2]), .C3(IB1_c0[3]));
  not not_1 (not_1_out, CLK);
  Register #(.width(4)) register_1 (.D(register_2_q), .en(Valid), .clk(CLK));  // open: Q, clr
  // Lock L1: pin names not known; wires that end beside it: IB1_c0, IB1_c0, IB1_c0, IB1_c0, IB1_c0, IB1_c0, CLK, L1_p8, L1_p9
  Counter #(.max('h7), .width(3)) counter_1 (
    .count(or_9_out), .Q(counter_1_q), .up(L1_p9), .clk(CLK));  // open: load, D, carry, clr
  or or_9 (or_9_out, L1_p8, L1_p9);
  Register #(.width(4)) register_2 (.D(register_3_q), .en(Valid), .clk(CLK), .Q(register_2_q));  // open: clr
  LED Unlocked (.in(and_1_out));
  and and_1 (and_1_out, ~counter_1_q[0], ~counter_1_q[1], ~counter_1_q[2]);  // AND_Gate
  Register #(.width(4)) register_3 (.D(register_4_q), .en(Valid), .clk(CLK), .Q(register_3_q));  // open: clr
  LED Locked (.in(and_2_out));
  and and_2 (and_2_out, ~counter_1_q[0], ~counter_1_q[1], counter_1_q[2]);  // AND_Gate
  Register #(.width(4)) register_4 (.D(register_5_q), .en(Valid), .clk(CLK), .Q(register_4_q));  // open: clr
  Register #(.width(4)) register_5 (.D(IB1_c0), .en(Valid), .clk(CLK), .Q(register_5_q));  // open: clr
endmodule

module Panel (
  input  R0,
  input  R1,
  input  R2,
  input  R3,
  input  C0,
  input  C1,
  input  C2,
  output B0,
  output B1,
  output B2,
  output B3,
  output V
);

  wire and_1_out, and_2_out, and_3_out, and_4_out, and_5_out, and_6_out, and_7_out, and_8_out, and_9_out,
       and_10_out, and_11_out, not_1_out, not_2_out, not_3_out, not_4_out, xor_1_out, xor_2_out, y0, y1, z0,
       z1;

  not not_1 (not_1_out, y0);
  not not_2 (not_2_out, y1);
  not not_3 (not_3_out, z0);
  or or_1 (y1, R1, R3);
  or or_2 (y0, R2, R3);
  or or_3 (z1, C0, C2);
  or or_4 (z0, C1, C2);
  not not_4 (not_4_out, z1);
  ExactlyOne xor_1 (.out(xor_1_out), .in0(R0), .in1(R1), .in2(R2), .in3(R3));
  ExactlyOne xor_2 (.out(xor_2_out), .in0(C0), .in1(C1), .in2(C2));
  and and_1 (and_1_out, y0, y1, z1);
  and and_2 (and_2_out, y0, not_2_out, z0);
  and and_3 (and_3_out, not_1_out, y1, z0);
  and and_4 (and_4_out, not_1_out, y1, not_3_out, z1);
  and and_5 (and_5_out, y0, not_2_out, not_3_out, z1);
  and and_6 (and_6_out, y0, not_3_out, z1);
  and and_7 (and_7_out, y1, z0, z1);
  and and_8 (and_8_out, not_1_out, not_2_out, z0);
  and and_9 (and_9_out, not_2_out, z1);
  and and_10 (and_10_out, y0, y1, z0, z1);
  and and_11 (and_11_out, not_1_out, y1, z0, not_4_out);
  and and_12 (V, xor_1_out, xor_2_out);
  or or_5 (B3, and_1_out, and_2_out);
  or or_6 (B2, and_3_out, and_4_out, and_5_out);
  or or_7 (B1, and_6_out, and_7_out, and_8_out);
  or or_8 (B0, and_9_out, and_10_out, and_11_out);
endmodule

module InputBuffer (
  input  B0,
  input  B1,
  input  B2,
  input  B3,
  input  V,
  input  CLK,
  output C0,
  output C1,
  output C2,
  output C3
);

  wire and_1_out, and_2_out, and_3_out, or_1_out, S, Y1_qn, Y2_q, Y2_qn;
  wire [3:0] not_1_out, register_1_q, register_2_q;

  Register #(.width(4)) register_1 (.Q(register_1_q));  // open: D, en, clk, clr
  Register #(.width(4)) register_2 (.D({B3, B2, B1, B0}), .en(V), .clk(CLK), .Q(register_2_q));  // open: clr
  assign not_1_out = ~register_1_q;  // NOT_Gate not_1, 4 bits wide
  and and_1 (and_1_out, Y2_q, V, Y1_qn);
  or or_1 (or_1_out, and_1_out, and_2_out);
  and and_2 (and_2_out, Y2_qn, V, S);
  and and_3 (and_3_out, Y2_qn, V, Y1_qn);
  Multiplexer #(.width(4)) multiplexer_1 (.in0(not_1_out), .in1(register_2_q), .out({C3, C2, C1, C0}), .sel(S));
  D_Flip_Flop Y2 (.D(or_1_out), .clk(CLK), .Q(Y2_q), .Qn(Y2_qn));  // open: preset, reset
  D_Flip_Flop Y1 (.D(and_3_out), .clk(CLK), .Q(S), .Qn(Y1_qn));  // open: preset, reset
endmodule

module Lock (
  input  C0,
  input  C1,
  input  C2,
  input  C3,
  input  CLK,
  input  in_6,
  input  in_7,
  output L,
  output U,
  output out_10,
  output [3:0] out_11,
  output s1,
  output s0,
  output out_14,
  output out_15,
  output y2,
  output out_17,
  output y1
);

  wire and_1_out, and_2_out, and_3_out, and_4_out, and_5_out, and_6_out, and_7_out, and_8_out, and_9_out,
       and_10_out, and_11_out, and_13_out, and_14_out, and_15_out, and_16_out, and_17_out, and_18_out,
       bigin1, bigin2, controlled_buffer_1_out, controlled_buffer_2_out, LCodeTwice_carry, Lsub1out,
       Lsub2out, nor_1_out, not_1_out, not_2_out, not_3_out, not_4_out, not_5_out, not_6_out, not_7_out,
       not_8_out, not_9_out, not_10_out, not_11_out, not_12_out, or_1_out, or_2_out, or_3_out, undriven,
       undriven_3, undriven_4, Usub1out, Usub2out, WE, xnor_1_out;
  wire [1:0] LCodeTwice_q, undriven_2;
  wire [3:0] R1_q, R2_q;

  Counter #(.max('h0), .width(2)) counter_1 (
    .load(undriven), .up(CLK), .clk(CLK), .D(undriven_2), .carry(out_17));  // open: clr, count, Q
  Clock clock_1 (.out(CLK));
  nand nand_1 (WE, C0, C1, C2, C3);
  nor nor_1 (nor_1_out, out_14, y1);
  assign controlled_buffer_1_out = nor_1_out ? s1 : 1'bz;  // Controlled_Buffer controlled_buffer_1
  assign controlled_buffer_2_out = nor_1_out ? s0 : 1'bz;  // Controlled_Buffer controlled_buffer_2
  not not_1 (not_1_out, Usub1out);
  not not_2 (not_2_out, Usub2out);
  not not_3 (not_3_out, controlled_buffer_1_out);
  not not_4 (not_4_out, C2);
  not not_5 (not_5_out, C0);
  not not_6 (not_6_out, not_2_out);
  and and_1 (and_1_out, C0, C1, C2, C3);
  and and_2 (and_2_out, C3, not_4_out, C1, C0);
  and and_3 (and_3_out, C3, not_4_out, C1, not_5_out);
  or or_1 (or_1_out, undriven_3, undriven_4);
  assign bigin2 = or_1_out ? out_15 : 1'bz;  // Controlled_Buffer controlled_buffer_3
  nor nor_2 (s1, and_1_out, and_3_out);
  nor nor_3 (s0, and_1_out, and_2_out);
  assign bigin1 = or_1_out ? out_14 : 1'bz;  // Controlled_Buffer controlled_buffer_4
  D_Flip_Flop State1 (.D(bigin1), .clk(out_17), .Q(out_14));  // open: Qn, preset, reset
  D_Flip_Flop State2 (.D(bigin2), .clk(out_17), .Q(y1));  // open: Qn, preset, reset
  and and_4 (and_4_out, controlled_buffer_1_out, controlled_buffer_2_out, not_1_out, Usub2out);
  and and_5 (and_5_out, controlled_buffer_2_out, controlled_buffer_1_out, Usub1out, not_2_out);
  and and_6 (and_6_out, Usub1out, controlled_buffer_2_out, not_3_out);
  and and_7 (and_7_out, not_2_out, not_3_out, controlled_buffer_2_out);
  and and_8 (and_8_out, not_6_out, Usub1out, controlled_buffer_2_out);
  not not_7 (not_7_out, s1);
  or or_2 (or_2_out, and_4_out, and_5_out);
  or or_3 (or_3_out, and_6_out, and_7_out, and_8_out);
  D_Flip_Flop Lsub1 (.clk(CLK), .Q(Lsub1out));  // open: D, Qn, preset, reset
  D_Flip_Flop Lsub2 (.clk(CLK), .Q(Lsub2out));  // open: D, Qn, preset, reset
  not not_8 (not_8_out, s0);
  D_Flip_Flop Usub1 (.D(or_2_out), .clk(CLK), .Q(Usub1out));  // open: Qn, preset, reset
  D_Flip_Flop Usub2 (.D(or_3_out), .clk(CLK), .Q(Usub2out));  // open: Qn, preset, reset
  not not_9 (not_9_out, s1);
  and and_9 (and_9_out, not_9_out, s0);
  not not_10 (not_10_out, out_14);
  and and_10 (and_10_out, not_10_out, not_11_out);
  not not_11 (not_11_out, y1);
  not not_12 (not_12_out, out_14);
  and and_11 (and_11_out, and_9_out, and_10_out);
  Counter #(.max('h2), .width(2)) LCodeTwice (
    .up(and_11_out), .clk(and_11_out), .carry(LCodeTwice_carry), .Q(LCodeTwice_q));  // open: clr, load, count, D
  xnor xnor_1 (xnor_1_out, Usub1out, Usub2out);
  and and_12 (bigin2, xnor_1_out, s0);
  Counter #(.max('h3), .width(2)) counter_2 (.load(out_10), .up(CLK), .clk(CLK));  // open: clr, count, D, carry, Q
  and and_13 (and_13_out, not_12_out, not_7_out, s0);
  and and_14 (and_14_out, not_12_out, y1, not_7_out, not_8_out);
  and and_15 (and_15_out, not_12_out, y1, s1, s0);
  and and_16 (and_16_out, out_14, s1, not_8_out);
  and and_17 (and_17_out, out_14, y1, not_8_out, not_7_out);
  and and_18 (and_18_out, out_14, s1, y1, s0);
  not not_13 (bigin1, bigin2);
  or or_4 (out_15, and_13_out, and_14_out, and_15_out, and_16_out, and_17_out, and_18_out);
  // AND_Gate and_19 has open pins: in0=LCodeTwice_q[0], in1=CLK, out=open
  // AND_Gate and_20 is placed but not wired
  Transistor #(.width(4)) transistor_1 (.in({C3, C2, C1, C0}), .gate(in_7));  // open: out
  Register #(.width(4)) R2 (.D({C3, C2, C1, C0}), .en(WE), .Q(R2_q), .clr(in_6));  // open: clk
  Register #(.width(4)) R1 (.D(R2_q), .en(WE), .Q(R1_q));  // open: clk, clr
  Register #(.width(4)) R0 (.D(R1_q), .en(WE), .Q(out_11));  // open: clk, clr

  assign y2 = out_14;

  // Other names for the same wires on the sheet: bigout1 = out_14; bigout2 = y1; I1 = s1; I2 = s0

  // Notes on the sheet:
  //   Lock= L=1 U=0 for 4 clock cycles.
  //   FIXME: delete later
  //   4bit to 2bit
  //   Unlocked to Locking
  //   Locked to Unlocking
  //   L code with unlocked state
  //   Next State
endmodule
